# Fritzing sketch oled+2sr+breadboard (saved by Fritzing 0.9.10b)
breadboards: 1

parts:
  Part1 = Arduino Nano 33 IOT
  OLED_I2C1 = OLED 128x64 I2C Monochrome Display
  U1 = 74HC595 [package="DIP16 [THT]"]
  LED1 = LED - 5mm [color="Red (633nm)" current=0.030 package="5 mm [THT]"]
  LED2 = LED - 5mm [color="Red (633nm)" current=0.030 package="5 mm [THT]"]
  R1 = Resistor Mini [tolerance=±5% resistance=220 package=THT]
  R2 = Resistor Mini [tolerance=±5% resistance=220 package=THT]
  R3 = Resistor Mini [tolerance=±5% resistance=220 package=THT]
  R4 = Resistor Mini [tolerance=±5% resistance=220 package=THT]
  R5 = Resistor Mini [tolerance=±5% resistance=220 package=THT]
  R6 = Resistor Mini [tolerance=±5% resistance=220 package=THT]
  R7 = Resistor Mini [tolerance=±5% resistance=220 package=THT]
  LED3 = LED - 5mm [color="Red (633nm)" current=0.030 package="5 mm [THT]"]
  LED4 = LED - 5mm [color="Red (633nm)" current=0.030 package="5 mm [THT]"]
  LED5 = LED - 5mm [color="Red (633nm)" current=0.030 package="5 mm [THT]"]
  LED6 = LED - 5mm [color="Red (633nm)" current=0.030 package="5 mm [THT]"]
  LED7 = LED - 5mm [color="Red (633nm)" current=0.030 package="5 mm [THT]"]
  R8 = Resistor Mini [tolerance=±5% resistance=220 package=THT]
  LED8 = LED - 5mm [color="Red (633nm)" current=0.030 package="5 mm [THT]"]
  U2 = 74HC595 [package="DIP16 [THT]"]
  R9 = Resistor Mini [tolerance=±5% resistance=220 package=THT]
  R10 = Resistor Mini [tolerance=±5% resistance=220 package=THT]
  R11 = Resistor Mini [tolerance=±5% resistance=220 package=THT]
  R12 = Resistor Mini [tolerance=±5% resistance=220 package=THT]
  R13 = Resistor Mini [tolerance=±5% resistance=220 package=THT]
  R14 = Resistor Mini [tolerance=±5% resistance=220 package=THT]
  R15 = Resistor Mini [tolerance=±5% resistance=220 package=THT]
  LED9 = LED - 5mm [color="Red (633nm)" current=0.030 package="5 mm [THT]"]
  LED10 = LED - 5mm [color="Red (633nm)" current=0.030 package="5 mm [THT]"]
  LED11 = LED - 5mm [color="Red (633nm)" current=0.030 package="5 mm [THT]"]
  LED12 = LED - 5mm [color="Red (633nm)" current=0.030 package="5 mm [THT]"]
  LED13 = LED - 5mm [color="Red (633nm)" current=0.030 package="5 mm [THT]"]
  LED14 = LED - 5mm [color="Red (633nm)" current=0.030 package="5 mm [THT]"]
  LED15 = LED - 5mm [color="Red (633nm)" current=0.030 package="5 mm [THT]"]
  R16 = Resistor Mini [tolerance=±5% resistance=220 package=THT]
  LED16 = LED - 5mm [color="Red (633nm)" current=0.030 package="5 mm [THT]"]

nets:
  N1: Part1.RESET, Part1.A7
  GND: Part1.GND, Part1.D13~, OLED_I2C1.GND, U1.GND, U1.OE, U2.GND, U2.OE
  N2: Part1.D4, U1.DS
  N3: Part1.D5~, U1.ST_CP, U2.ST_CP
  N4: Part1.D6~, U1.SH_CP, U2.SH_CP
  N5: Part1.D11/MOSI, Part1.+5V
  VCC: Part1.VIN, U1.MR, U1.VCC, U2.MR, U2.VCC
  N6: Part1.A5, OLED_I2C1.SCK
  N7: Part1.A4, OLED_I2C1.SDA
  3V3: Part1.3V3, OLED_I2C1.VDD, LED1.anode, LED2.anode, LED3.anode, LED4.anode, LED5.anode, LED6.anode, LED7.anode, LED8.anode, LED9.anode, LED10.anode, LED11.anode, LED12.anode, LED13.anode, LED14.anode, LED15.anode, LED16.anode
  N8: U1.Q1, R1.Pin_0, R1.Pin_1
  N9: U1.Q2, LED2.cathode, R2.Pin_0, R2.Pin_1
  N10: U1.Q3, R3.Pin_0, R3.Pin_1, LED3.cathode
  N11: U1.Q4, R4.Pin_0, R4.Pin_1, LED4.cathode
  N12: U1.Q5, R5.Pin_0, R5.Pin_1, LED5.cathode
  N13: U1.Q6, R6.Pin_0, R6.Pin_1, LED6.cathode
  N14: U1.Q7, R7.Pin_0, R7.Pin_1, LED7.cathode
  N15: U1.Q7', U2.DS
  N16: U1.Q0, R8.Pin_0, R8.Pin_1, LED8.cathode
  N17: U2.Q1, R9.Pin_0, R9.Pin_1, LED9.cathode
  N18: U2.Q2, R10.Pin_0, R10.Pin_1, LED10.cathode
  N19: U2.Q3, R11.Pin_0, R11.Pin_1, LED11.cathode
  N20: U2.Q4, R12.Pin_0, R12.Pin_1, LED12.cathode
  N21: U2.Q5, R13.Pin_0, R13.Pin_1, LED13.cathode
  N22: U2.Q6, R14.Pin_0, R14.Pin_1, LED14.cathode
  N23: U2.Q7, R15.Pin_0, R15.Pin_1, LED15.cathode
  N24: U2.Q0, R16.Pin_0, R16.Pin_1, LED16.cathode

notes:
  Blue - OLED to Arduino
  Yellow - SR1 to Arduino
  Blue - SR2 to SR1

custom parts:
  Arduino Nano 33 IOT: The Arduino Nano 33 IoT is the easiest and cheapest point of entry to enhance existing devices (and creating new ones) to be part of the IoT and designing pico-network applications. Whether you are looking at building a sensor network connected to your office or home router, or if you want to create a BLE device sending data to a cellphone, the Nano 33 IoT is your one-stop-solution for many of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
  Resistor Mini: A generic resistor (0.25W)
